# Fritzing sketch 3.3V-Regulator (saved by Fritzing 0.9.3b)
breadboards: 1

parts:
  LP3874-ADJ = Voltage Regulator LDO [package=sot23-5]
  C1 = Ceramic Capacitor [capacitance=47pF package="100 mil [THT, multilayer]"]
  C3 = Electrolytic Capacitor [capacitance=10µF package="100 mil [THT, electrolytic]"]
  C4 = Tantalum Capacitor [capacitance=10µF package="100 mil [THT, tantalum]"]
  R1 = Resistor [tolerance=±10% resistance=83k package=THT]
  R2 = Resistor [tolerance=±10% resistance=47k package=THT]
  R3 = Resistor [tolerance=±10% resistance=47k package=THT]

nets:
  5V: LP3874-ADJ.IN, C4.+, R3.Pin_1
  GND: LP3874-ADJ.GND, C3.-, R2.Pin_0
  N1: LP3874-ADJ.EN, R3.Pin_0
  N2: LP3874-ADJ.BP, C1.0, R1.Pin_0, R2.Pin_1
  3.3V: LP3874-ADJ.OUT, C1.1, C3.+, R1.Pin_1
