# Fritzing sketch LED_flasher (saved by Fritzing 0.9.3b)
breadboards: 1

parts:
  LED1 = LED - 5mm [color="Red (633nm)" package="5 mm [THT]"]
  LED2 = LED - 5mm [color="Red (633nm)" package="5 mm [THT]"]
  LED3 = LED - 5mm [color="Red (633nm)" package="5 mm [THT]"]
  LED4 = LED - 5mm [color="Red (633nm)" package="5 mm [THT]"]
  LED5 = LED - 5mm [color="Red (633nm)" package="5 mm [THT]"]
  R1 = Resistor [tolerance=±5% resistance=220 package=THT]
  J1 = Screw terminal - 2 pins [package=THT]
  J2 = Screw terminal - 2 pins [package=THT]
  Q1 = Basic FET N-Channel [package="DPak [SMD]"]

nets:
  N1: LED1.cathode, LED2.anode
  N2: LED1.anode, LED4.cathode
  N3: LED2.cathode, LED3.anode
  N4: LED3.cathode, J2.pin2
  N5: LED4.anode, LED5.cathode
  N6: LED5.anode, R1.Pin_0
  N7: R1.Pin_1, J2.pin1
  12V: J1.pin1
  N8: J1.pin2, Q1.drain
  GND: Q1.source

notes:
  12V LED
  Module
  modules attached
  in parallel
