# Fritzing sketch MCU-arduino_pro_mini (saved by Fritzing 0.9.3b)
breadboards: 1

parts:
  Mini_Pro = Arduino Mini (Rev5)
  Part4 = Arduino Micro (Rev3)  # not connected

nets:
  RX: Mini_Pro.D1/RX, Mini_Pro.RX
  address2: Mini_Pro.RESET
  net label: Mini_Pro.D2
  PIR: Mini_Pro.D3_PWM
  temperature: Mini_Pro.D4
  address0: Mini_Pro.D5_PWM
  address1: Mini_Pro.D6_PWM
  address3: Mini_Pro.D8
  relay0: Mini_Pro.D9_PWM
  relay3: Mini_Pro.A3
  soil: Mini_Pro.A2
  relay2: Mini_Pro.A1
  relay1: Mini_Pro.A0
  SCLK: Mini_Pro.D13
  MISO: Mini_Pro.D12
  MOSI: Mini_Pro.D11_PWM
  SS: Mini_Pro.D10_PWM
  light: Mini_Pro.A6
  switch0: Mini_Pro.A4
  water: Mini_Pro.A7
  switch1: Mini_Pro.A5
  TX: Mini_Pro.TX
  GND: Mini_Pro.GND
  5V: Mini_Pro.5V
