# Fritzing sketch PIR_360_degrees_sensor (saved by Fritzing 0.9.3b)
breadboards: 1

parts:
  PIR1 = PIR sensor
  PIR2 = PIR sensor
  PIR3 = PIR sensor
  PIR4 = PIR sensor
  switching = Rectifier Diode [part_number=1N4001 package="300 mil [THT]"]
  switching1 = Rectifier Diode [part_number=1N4001 package="300 mil [THT]"]
  switching2 = Rectifier Diode [part_number=1N4001 package="300 mil [THT]"]
  switching3 = Rectifier Diode [part_number=1N4001 package="300 mil [THT]"]
  R1 = Resistor [tolerance=±5% resistance=470k package=THT]

nets:
  5V: PIR1.VDD, PIR2.VDD, PIR3.VDD, PIR4.VDD
  N1: PIR1.SIG, switching.anode
  GND: PIR1.GND, PIR2.GND, PIR3.GND, PIR4.GND, R1.Pin_0
  N2: PIR2.SIG, switching3.anode
  N3: PIR3.SIG, switching2.anode
  N4: PIR4.SIG, switching1.anode
  pir: switching.cathode, switching1.cathode, switching2.cathode, switching3.cathode, R1.Pin_1
