# Fritzing sketch RFM69-radio (saved by Fritzing 0.9.3b)
breadboards: 1

parts:
  U1 = Voltage Regulator - 3.3V [package="TO220 [THT]"]  # not connected
  RFM69HW = RFM69HCW ISM Transciever
  Bidirectional_Level_converter = Logic Level Converter
  Antenna = Chip antenna [package=antenna-chip4]

nets:
  GND: RFM69HW.1_GND, RFM69HW.8_GND, Bidirectional_Level_converter.GND
  N1: RFM69HW.2_MISO, Bidirectional_Level_converter.RX_HV
  N2: RFM69HW.3_MOSI, Bidirectional_Level_converter.RX2_HV
  N3: RFM69HW.4_SCK, Bidirectional_Level_converter.TX2_LV
  N4: RFM69HW.5_NSS_(CS), Bidirectional_Level_converter.TX_LV
  N5: RFM69HW.9_ANT, Antenna.SIGNAL
  3.3V: RFM69HW.13_3.3V, Bidirectional_Level_converter.LV
  RFIO: RFM69HW.14_DIO0
  MOSI: Bidirectional_Level_converter.RX2_LV
  MISO: Bidirectional_Level_converter.RX_LV
  SS: Bidirectional_Level_converter.TX_HV
  5V: Bidirectional_Level_converter.HV
  SCK: Bidirectional_Level_converter.TX2_HV

custom parts:
  RFM69HCW ISM Transciever: RF Transceiver by Hope RF. Well supported Arduino libraries are available. This ISM band transceiver is available in several frequencies e.g. 433MHz and 915MHz and it is also available in various feature versions.
