# Fritzing sketch address_circuit (saved by Fritzing 0.9.3b)
breadboards: 1

parts:
  JP3 = Header 4 [package=1x04-smd]
  JP4 = Header 4 [package=1x04-smd]

nets:
  address0: JP3.1
  address1: JP3.2
  address2: JP3.3
  address3: JP3.4
  GND: JP4.1, JP4.2, JP4.3, JP4.4

notes:
  jumpers, solder, or switches
