# Fritzing sketch bed_ocupancy_sensor (saved by Fritzing 0.9.3b)
breadboards: 1

parts:
  J1 = LOAD_CELL [package=1x03]
  J2 = LOAD_CELL [package=1x03]
  J3 = LOAD_CELL [package=1x03]
  J4 = LOAD_CELL [package=1x03]
  U1 = AD8226 - Rail-to-Rail output Instrumentation Amplifier [part_number=AD8226]
  LT1013 = OPA344 [package=sot23-5]
  R1 = Resistor [tolerance=±5% resistance=220 package=THT]
  C1 = Ceramic Capacitor [capacitance=100nF package="100 mil [THT, multilayer]"]
  C2 = Tantalum Capacitor [capacitance=1μF package="100 mil [THT, tantalum]"]
  C3 = Ceramic Capacitor [capacitance=100nF package="100 mil [THT, multilayer]"]
  C4 = Tantalum Capacitor [capacitance=1μF package="100 mil [THT, tantalum]"]

nets:
  N1: J1.B, J3.B
  GND: J1.W, U1.-VS, C1.0, C2.-, C3.0, C4.-
  N2: J1.R, J2.R
  N3: J2.B, J4.B
  N4: J2.W, U1.+IN
  N5: J3.W, U1.-IN
  N6: J3.R, J4.R
  5V: J4.W, U1.+VS, C3.1
  N7: U1.RG#2, R1.Pin_1
  N8: U1.RG#3, R1.Pin_0
  net label: LT1013.OUT
  N9: C1.1, C2.+

notes:
  white
  black
  red
