# Fritzing sketch light_sensor (saved by Fritzing 0.9.3b)
breadboards: 1

parts:
  R2 = PHOTOCELL [package=photocell]
  R3 = Resistor [tolerance=±5% resistance=10k package=THT]

nets:
  5V: R2.P$1
  light: R2.P$2, R3.Pin_0
  GND: R3.Pin_1
