# Fritzing sketch relay_array-ceilling_fan (saved by Fritzing 0.9.3b)
breadboards: 1

parts:
  light_relay = RELAY [package=relay-jzc]
  fan_high_relay = RELAY [package=relay-jzc]
  fan_low_relay = RELAY [package=relay-jzc]
  fan_med_relay = RELAY [package=relay-jzc]
  D1 = Rectifier Diode [part_number=1N4001 package="Melf DO-213 AB [SMD]"]
  D2 = Rectifier Diode [part_number=1N4001 package="Melf DO-213 AB [SMD]"]
  D3 = Rectifier Diode [part_number=1N4001 package="Melf DO-213 AB [SMD]"]
  D4 = Rectifier Diode [part_number=1N4001 package="Melf DO-213 AB [SMD]"]
  low = DC Motor
  med = DC Motor
  high = DC Motor
  LED1 = LED - 5mm [color="Red (633nm)" package="5 mm [THT]"]
  Light_bulb = Bulb holder (E10) with base
  fan_speed_control = SWITCH-SP3T [package=switch-sp3t-smd]
  C1 = Ceramic Capacitor [capacitance=100nF package="200 mil [THT, multilayer]"]
  U1 = SWITCH-SPST-2 [package=switch-spst-vertical]
  R1 = Resistor [tolerance=±5% resistance=470 package=THT]
  LED2 = LED - 5mm [color="Red (633nm)" package="5 mm [THT]"]
  R2 = Resistor [tolerance=±5% resistance=470 package=THT]
  LED3 = LED - 5mm [color="Red (633nm)" package="5 mm [THT]"]
  R3 = Resistor [tolerance=±5% resistance=470 package=THT]
  J1 = screw terminal, 6 pins
  J2 = screw terminal, 6 pins

nets:
  GND: light_relay.COIL2
  N1: light_relay.NO, J1.pin6
  N2: light_relay.MAIN, J1.pin5
  light: light_relay.COIL1, D1.cathode
  N3: fan_high_relay.COIL2, fan_low_relay.COIL2, fan_med_relay.COIL2, LED1.cathode, LED2.cathode, LED3.cathode
  N4: fan_high_relay.NO, J1.pin4
  N5: fan_high_relay.MAIN, fan_low_relay.MAIN, fan_med_relay.MAIN, J1.pin1
  N6: fan_high_relay.COIL1, D2.cathode
  N7: fan_low_relay.NO, J1.pin2
  N8: fan_med_relay.NO, J1.pin3
  fan low: D3.cathode, R1.Pin_1
  fan med: D4.cathode, R2.Pin_1
  N9: low.pin_1, fan_speed_control.4, J2.pin2
  N10: low.pin_2, med.pin_2, high.pin_2, C1.1
  N11: med.pin_1, fan_speed_control.2
  N12: high.pin_1, fan_speed_control.1, J2.pin4
  N13: LED1.anode, R1.Pin_0
  N14: Light_bulb.pin_1, U1.O, J2.pin5
  AC neutral: Light_bulb.pin_2, C1.0
  AC fan power: fan_speed_control.3, J2.pin1
  AC light power: U1.P, J2.pin6
  N15: LED2.anode, R2.Pin_0
  N16: LED3.anode, R3.Pin_0
  fan high: R3.Pin_1

notes:
  switch
  Fan
  Motor
  Relays bypass fans
  switches
  Ceiling Fan circuitry

custom parts:
  Bulb holder (E10) with base: A bulb holder for an E10 bulb with a base.
