# Fritzing sketch relay_array (saved by Fritzing 0.9.3b)
breadboards: 1

parts:
  3 = RELAY [package=relay-jzc]
  2 = RELAY [package=relay-jzc]
  0 = RELAY [package=relay-jzc]
  1 = RELAY [package=relay-jzc]
  D1 = Rectifier Diode [part_number=1N4001 package="Melf DO-213 AB [SMD]"]  # not connected
  D2 = Rectifier Diode [part_number=1N4001 package="Melf DO-213 AB [SMD]"]  # not connected
  D3 = Rectifier Diode [part_number=1N4001 package="Melf DO-213 AB [SMD]"]  # not connected
  D4 = Rectifier Diode [part_number=1N4001 package="Melf DO-213 AB [SMD]"]  # not connected
  J4 = screw terminal, 8 pins

nets:
  GND: 3.COIL2
  N1: 3.NO, J4.pin8
  N2: 3.MAIN, J4.pin7
  relay3: 3.COIL1
  N3: 2.COIL2, 0.COIL2, 1.COIL2
  N4: 2.NO, J4.pin6
  N5: 2.MAIN, J4.pin5
  relay2: 2.COIL1
  N6: 0.NO, J4.pin2
  N7: 0.MAIN, J4.pin1
  relay0: 0.COIL1
  N8: 1.NO, J4.pin4
  N9: 1.MAIN, J4.pin3
  relay1: 1.COIL1
