# Fritzing sketch temperature_humidity_sensor-DHT22 (saved by Fritzing 0.9.3b)
breadboards: 1

parts:
  R1 = Resistor [tolerance=±5% resistance=4.7k package=THT]
  DHT22 = Humidity and Temperature Sensor RHT03

nets:
  5V: R1.Pin_1, DHT22.Vcc
  temperature: DHT22.Data-signal
  GND: DHT22.GND_1
