# Fritzing sketch temperature_sensor-DS18B20 (saved by Fritzing 0.9.3b)
breadboards: 1

parts:
  part = DS18B20 1-Wire Temperature Sensor [part_number=DS18B20]
  R1 = Resistor [tolerance=±5% resistance=4.7k package=THT]

nets:
  5V: part.VDD, R1.Pin_1
  temperature: part.DQ
  GND: part.GND
